# Fritzing sketch equilibrista (saved by Fritzing 0.9.10b)
perfboards: 1

parts:
  J3 = Piezo Speaker  # not connected
  U6 = LuaNode32 / ESP32
  Componente10 = Motor Driver 1A Dual TB6612FNG
  TRM19 = Borne kre 2 vias
  U7 = LM2596 step down module
  S3 = Toggle Switch [package=THT]
  Componente11 = InvenSense MPU6050
  TRM20 = Terminal 2pin
  TRM22 = Terminal 2pin
  TRM23 = Terminal 2pin
  TRM24 = Terminal 2pin
  TRM25 = Terminal 2pin
  TRM21 = Terminal 2pin

nets:
  N1: U6.D34, Componente10.PWMA
  N2: U6.D35, Componente10.AIN2
  N3: U6.D32, Componente10.AIN1
  N4: U6.D33, Componente10.STBY
  N5: U6.D25, Componente10.BIN1
  N6: U6.D26, Componente10.BIN2
  N7: U6.D27, Componente10.PWMB
  N8: U6.D12, TRM22.pin_2
  N9: U6.D13, TRM22.pin_1
  N10: U6.GND, TRM19.pin_2, U7.IN-, U7.OUT-, TRM25.pin_2, TRM21.pin_1
  N11: U6.Vin, Componente10.VM, U7.OUT+
  N12: U6.3V3, TRM20.pin_2
  N13: U6.D21, Componente11.SDA
  N14: U6.D22, Componente11.SCL
  N15: U6.D23, TRM23.pin_2
  N16: Componente10.B01, TRM20.pin_1
  N17: Componente10.B02, TRM21.pin_2
  N18: Componente10.A02, TRM25.pin_1
  N19: Componente10.A01, TRM24.pin_2
  N20: TRM19.pin_1, S3.L2
  N21: U7.IN+, S3.COM
  N22: Componente11.VCC, TRM24.pin_1

custom parts:
  LuaNode32 / ESP32: ESP32 based LuaNode32
  Borne kre 2 vias: 2-pin Terminal Block
  LM2596 step down module: LM2596 DC-DC step down power supply module 3 A.
  Terminal 2pin: 2-pin Terminal Block
